# Fritzing sketch tiny_iambic_decoder_bb (saved by Fritzing 0.9.10b)
breadboards: 1

parts:
  U1 = attiny85 [package=dip]
  S1 = Pushbutton [package="[THT]"]
  S2 = Pushbutton [package="[THT]"]
  R1 = Vertical Resistor [tolerance=±5% resistance=4.7k package=THT]
  C1 = Film/Foil Capacitor [capacitance=100nF voltage=35V package="5mm [THT, pp]"]
  R2 = Vertical Resistor [tolerance=±5% resistance=4.7k package=THT]
  C2 = Film/Foil Capacitor [capacitance=100nF voltage=35V package="5mm [THT, pp]"]
  LED1 = LED - 3mm [color="Red (633nm)" current=0.030 package="3 mm [THT]"]
  R3 = Vertical Resistor [tolerance=±5% resistance=220 package=THT]
  SPKR1 = Loudspeaker
  Mod1 = KY-019 5V Relay Module [package="Breakout board"]

nets:
  N1: U1.Pin_2, S2.Pin_1, S2.Pin_2
  N2: U1.Pin_3, S1.Pin_1, S1.Pin_2
  N3: U1.Pin_5, R1.Pin_0
  N4: U1.Pin_7, Mod1.S
  N5: U1.Pin_8, R3.Pin_0, Mod1.+
  N6: S1.Pin_3, S1.Pin_4, S2.Pin_3, S2.Pin_4, C1.+, C2.+, SPKR1.pin1, Mod1.-, Mod1.Common
  N7: R1.Pin_1, C1.-, R2.Pin_0
  N8: R2.Pin_1, C2.-, SPKR1.pin2
  N9: LED1.cathode, Mod1.NO
  N10: LED1.anode, R3.Pin_1

notes:
  Dot
  Dash
  PWM audio output filter
  Keying output (connect to transmitter)
  Buttons simulating dual lever paddle
  Led for testing keying output status
  Audio output (dit and dah)

custom parts:
  Vertical Resistor: A generic resistor (0.25W)
  KY-019 5V Relay Module: KY-019 5V Relay module, used to control AC circuits. (Special thanks to vanepp for fixing the PCB holes and other errors)
